// Logisim project ALU.circ as structural Verilog: 2 circuits, main circuit main
module main (
  input  carry,
  input  [7:0] a,
  input  [7:0] b,
  input  [3:0] in_4,
  output carry_out,
  output [7:0] out
);

  wire [7:0] adder_1_out, adder_2_out, adder_3_out, and_1_out, divider_1_out, multiplexer_1_out,
       multiplier_1_out, nand_1_out, nor_1_out, not_1_out, not_2_out, or_1_out, shifter_1_out, shifter_2_out,
       shifter_3_out, xnor_1_out, xor_1_out;

  assign not_1_out = ~b;  // NOT_Gate not_1, 8 bits wide
  Adder adder_1 (.a(not_1_out), .b(8'h1), .out(adder_1_out), .cin(1'b0));  // open: cout
  Multiplexer #(.width(8), .enable("false")) multiplexer_1 (
    .in0(b), .in1(adder_1_out), .out(multiplexer_1_out), .sel(in_4[1]));
  Adder adder_2 (.a(a), .b(multiplexer_1_out), .out(adder_2_out), .cin(carry), .cout(carry_out));
  assign and_1_out = a & b;  // AND_Gate and_1, 8 bits wide
  assign or_1_out = a | b;  // OR_Gate or_1, 8 bits wide
  assign xor_1_out = a ^ b;  // XOR_Gate xor_1, 8 bits wide
  assign nand_1_out = ~(a & b);  // NAND_Gate nand_1, 8 bits wide
  assign nor_1_out = ~(a | b);  // NOR_Gate nor_1, 8 bits wide
  assign xnor_1_out = ~(a ^ b);  // XNOR_Gate xnor_1, 8 bits wide
  assign not_2_out = ~a;  // NOT_Gate not_2, 8 bits wide
  Adder adder_3 (.a(a), .b(8'h1), .out(adder_3_out), .cin(1'b0));  // open: cout
  Shifter shifter_1 (.in(a), .\dist (b[2:0]), .out(shifter_1_out));
  Shifter #(.shift("lr")) shifter_2 (.in(a), .\dist (b[2:0]), .out(shifter_2_out));
  Shifter #(.shift("ar")) shifter_3 (.in(a), .\dist (b[2:0]), .out(shifter_3_out));
  Multiplier multiplier_1 (.a(a), .b(b), .out(multiplier_1_out));  // open: cin, cout
  Divider divider_1 (.a(a), .b(b), .out(divider_1_out));  // open: upper, rem
  Multiplexer #(.select(4), .width(8), .enable("false")) multiplexer_2 (
    .in0(adder_2_out), .in1(and_1_out), .in2(adder_2_out), .in3(or_1_out), .in4(xor_1_out), .in5(nand_1_out),
    .in6(nor_1_out), .in7(xnor_1_out), .in8(not_2_out), .in9(adder_3_out), .in10(shifter_1_out),
    .in11(shifter_2_out), .in12(shifter_3_out), .in13(multiplier_1_out), .in14(divider_1_out), .in15(b),
    .out(out), .sel(in_4));

  // Other names for the same wires on the sheet: opcode[3:0] = in_4
endmodule

module adder (
  input  carry_in,
  input  [7:0] a,
  input  [7:0] b,
  output [7:0] out,
  output carry_out
);

  Adder adder_1 (.a(a), .b(b), .out(out), .cin(carry_in), .cout(carry_out));
endmodule
