// Logisim project DiceGame.circ as structural Verilog: 4 circuits, main circuit main
// a
module main (
  output [3:0] out_1,
  output out_2,
  output out_3
);

  wire a, clock_1_out, clock_2_out, comparator_1_eq, controlled_buffer_1_out,
       point_register_controller_1_out, RESET, Test_logic_d2_3_12, Test_logic_d7, Test_logic_d7_11;
  wire [3:0] adder_1_out, adder_2_out, adder_3_out, counter_1_q, counter_2_q, point_register_q;

  Clock clock_1 (.out(clock_1_out));
  assign controlled_buffer_1_out = a ? clock_1_out : 1'bz;  // Controlled_Buffer controlled_buffer_1
  Button button_1 (.out(a));
  Counter #(.width(4), .max('h5)) counter_1 (
    .Q(counter_1_q), .clk(clock_2_out), .clr(RESET));  // open: load, D, count, carry
  Clock clock_2 (.out(clock_2_out));
  Counter #(.width(4), .max('h5)) counter_2 (
    .Q(counter_2_q), .clk(controlled_buffer_1_out), .clr(RESET));  // open: load, D, count, carry
  Adder #(.width(4)) adder_1 (.a(counter_1_q), .b(4'b0001), .out(adder_1_out));  // open: cin, cout
  Adder #(.width(4)) adder_2 (.a(counter_2_q), .b(4'b0001), .out(adder_2_out));  // open: cin, cout
  Button button_2 (.out(RESET));
  Hex_Digit_Display hex_digit_display_1 (.value(adder_1_out));  // open: dp
  Hex_Digit_Display hex_digit_display_2 (.value(adder_2_out));  // open: dp
  Adder #(.width(4)) adder_3 (.a(adder_1_out), .b(adder_2_out), .out(adder_3_out));  // open: cin, cout
  point_register_controller point_register_controller_1 (.IN(a), .RESET(RESET), .OUT(point_register_controller_1_out));
  Register #(.width(4), .trigger("falling")) register_1 (.D(adder_3_out), .Q(out_1), .clk(a), .clr(RESET));  // open: en
  Register #(.width(4)) point_register (
    .D(adder_3_out), .Q(point_register_q), .clk(point_register_controller_1_out), .clr(RESET));  // open: en
  Test_logic Test_logic (.in_1(out_1), .D7(Test_logic_d7), .D7_11(Test_logic_d7_11), .D2_3_12(Test_logic_d2_3_12));
  Comparator #(.width(4), .mode("unsigned")) comparator_1 (
    .a(out_1), .b(point_register_q), .eq(comparator_1_eq));  // open: gt, lt
  controller Controller (
    .BUTTON(a), .in_2(RESET), .D7(Test_logic_d7), .D7_11(Test_logic_d7_11), .D2_3_12(Test_logic_d2_3_12),
    .C(comparator_1_eq), .W(out_2), .L(out_3));
endmodule

module Test_logic (
  input  [3:0] in_1,
  output D7,
  output D7_11,
  output D2_3_12
);

  wire comparator_2_eq, comparator_3_eq, comparator_4_eq, comparator_5_eq;

  Comparator #(.width(4)) comparator_1 (.a(in_1), .b(4'b0111), .eq(D7));  // open: gt, lt
  Comparator #(.width(4)) comparator_2 (.a(in_1), .b(4'b1011), .eq(comparator_2_eq));  // open: gt, lt
  Comparator #(.width(4)) comparator_3 (.a(in_1), .b(4'b0010), .eq(comparator_3_eq));  // open: gt, lt
  Comparator #(.width(4)) comparator_4 (.a(in_1), .b(4'b0011), .eq(comparator_4_eq));  // open: gt, lt
  Comparator #(.width(4)) comparator_5 (.a(in_1), .b(4'b1100), .eq(comparator_5_eq));  // open: gt, lt
  or or_1 (D7_11, D7, comparator_2_eq);
  or or_2 (D2_3_12, comparator_3_eq, comparator_4_eq, comparator_5_eq);
endmodule

module point_register_controller (
  input  IN,
  input  RESET,
  output OUT
);

  wire and_1_out, and_2_out, and_3_out, and_4_out, clock_1_out, IN_prime, or_1_out, or_2_out, Q1, Q1_prime,
       Q2, Q2_prime;

  not not_1 (IN_prime, IN);
  and and_1 (and_1_out, IN_prime, Q2);
  nand nand_1 (OUT, IN, Q1_prime, Q2);
  Clock clock_1 (.out(clock_1_out));
  or or_1 (or_1_out, and_1_out, Q1);
  D_Flip_Flop d_ff_1 (.clk(clock_1_out), .D(or_1_out), .Q(Q1), .Qn(Q1_prime), .reset(RESET));  // open: preset, en
  and and_2 (and_2_out, IN, Q1_prime);
  and and_3 (and_3_out, Q2, Q1_prime);
  and and_4 (and_4_out, IN_prime, Q1);
  or or_2 (or_2_out, and_2_out, and_3_out, and_4_out);
  D_Flip_Flop d_ff_2 (.clk(clock_1_out), .D(or_2_out), .Q(Q2), .Qn(Q2_prime), .reset(RESET));  // open: preset, en
endmodule

module controller (
  input  BUTTON,
  input  in_2,
  input  D7,
  input  D7_11,
  input  D2_3_12,
  input  C,
  output W,
  output L
);

  wire _0, _1, _2, and_1_out, and_2_out, and_3_out, and_4_out, and_7_out, and_8_out, clock_1_out, G2, G3, G4,
       G5, not_1_out, not_2_out, or_1_out, or_2_out, or_3_out, S0, S0_prime, S1_prime, S2_prime, S3, S3_prime;
  wire [7:0] counter_1_q;

  Clock clock_1 (.out(clock_1_out));
  D_Flip_Flop #(.trigger("falling")) d_ff_1 (
    .clk(clock_1_out), .D(G2), .Q(S0), .Qn(S0_prime), .preset(in_2));  // open: en, reset
  and and_1 (and_1_out, D7_11, S0);
  and and_2 (and_2_out, C, S3);
  not not_1 (not_1_out, D7_11);
  and and_3 (and_3_out, not_1_out, S0);
  not not_2 (not_2_out, D2_3_12);
  and and_4 (and_4_out, not_2_out, S0);
  or or_1 (or_1_out, and_1_out, and_2_out, W);
  or or_2 (or_2_out, and_3_out, and_4_out, S3);
  D_Flip_Flop #(.trigger("falling")) d_ff_2 (
    .clk(clock_1_out), .D(G3), .Q(W), .Qn(S1_prime), .reset(in_2));  // open: preset, en
  and and_5 (G3, or_1_out, _2);
  and and_6 (G5, S1_prime, _1, or_2_out, S2_prime);
  Counter #(.trigger("falling")) counter_1 (.Q(counter_1_q), .clk(BUTTON), .clr(in_2));  // open: load, D, count, carry
  D_Flip_Flop #(.trigger("falling")) d_ff_3 (
    .clk(clock_1_out), .D(G4), .Q(L), .Qn(S2_prime), .reset(in_2));  // open: preset, en
  and and_7 (and_7_out, D2_3_12, S0);
  and and_8 (and_8_out, D7, S3);
  or or_3 (or_3_out, and_7_out, and_8_out, L);
  Comparator #(.mode("unsigned")) comparator_1 (.a(counter_1_q), .b({8{1'b0}}), .gt(_1), .eq(_0));  // open: lt
  Comparator #(.mode("unsigned")) comparator_2 (.a(counter_1_q), .b(8'h1), .gt(_2));  // open: eq, lt
  D_Flip_Flop #(.trigger("falling")) d_ff_4 (
    .clk(clock_1_out), .D(G5), .Q(S3), .Qn(S3_prime), .reset(in_2));  // open: preset, en
  and and_9 (G4, or_3_out, _2);
  and and_10 (G2, S0, S1_prime, _0, S2_prime, S3_prime);

  // Other names for the same wires on the sheet: reset = in_2; S1 = W; S2 = L
endmodule
